// Logisim project ExecuteBootleg.circ as structural Verilog: 8 circuits, main circuit main
module main (
  input  [3:0] icode,
  input  [3:0] ifun,
  input  [63:0] ValA,
  input  [63:0] ValB,
  input  [63:0] ValC,
  output [63:0] ValE,
  output [63:0] PCUpdate
);

  wire setcc_1_sccout;
  wire [2:0] alufun_1_nocodenofun;
  wire [63:0] ctrlogic_1_a, ctrlogic_1_b;

  CTRLogic ctrlogic_1 (.icode(icode), .valA(ValA), .valB(ValB), .valC(ValC), .A(ctrlogic_1_a), .B(ctrlogic_1_b));
  ALUfun alufun_1 (.icode(icode), .ifun(ifun), .noCodeNoFun(alufun_1_nocodenofun));
  setCC setcc_1 (.icode(icode), .SCCout(setcc_1_sccout));
  CC cc_1 (.setCC(setcc_1_sccout), .valE(ValE), .PCUpdate(PCUpdate));
  ALU alu_1 (.A(ctrlogic_1_a), .B(ctrlogic_1_b), .notFun(alufun_1_nocodenofun), .valE(ValE));
endmodule

module ALU (
  input  [63:0] A,
  input  [63:0] B,
  input  [2:0] notFun,
  output [63:0] valE
);

  wire [1:0] controlled_buffer_1_out;
  wire [63:0] adder_1_out, and_1_out, subtractor_1_out, xor_1_out;

  assign controlled_buffer_1_out = notFun[0] ? notFun[2:1] : 2'bz;  // Controlled_Buffer controlled_buffer_1
  Adder #(.width(64)) adder_1 (.a(A), .b(B), .out(adder_1_out));  // open: cin, cout
  Subtractor #(.width(64)) subtractor_1 (.a(A), .b(B), .out(subtractor_1_out));  // open: bin, bout
  assign and_1_out = A & B;  // AND_Gate and_1, 64 bits wide
  assign xor_1_out = A ^ B;  // XOR_Gate xor_1, 64 bits wide
  Multiplexer #(.select(2), .width(64)) multiplexer_1 (
    .in0(adder_1_out), .in1(subtractor_1_out), .in2(and_1_out), .in3(xor_1_out), .out(valE),
    .sel(controlled_buffer_1_out));
endmodule

module CTRLogic (
  input  [3:0] icode,
  input  [63:0] valA,
  input  [63:0] valB,
  input  [63:0] valC,
  output [63:0] A,
  output [63:0] B
);

  ALUB alub_1 (.icode(icode), .valB(valB), .B(B));
  ALUA alua_1 (.icode(icode), .valA(valA), .valC(valC), .A(A));
endmodule

module ALUA (
  input  [3:0] icode,
  input  [63:0] valA,
  input  [63:0] valC,
  output [63:0] A
);
endmodule

module ALUB (
  input  [3:0] icode,
  input  [63:0] valB,
  output [63:0] B
);
endmodule

module ALUfun (
  input  [3:0] icode,
  input  [3:0] ifun,
  output [2:0] noCodeNoFun
);

  wire not_1_out, not_2_out;

  not not_1 (not_1_out, icode[0]);
  not not_2 (not_2_out, icode[3]);
  and and_1 (noCodeNoFun[0], icode[1], not_1_out, not_2_out, icode[2]);

  assign noCodeNoFun[2:1] = ifun[1:0];
endmodule

module setCC (
  input  [3:0] icode,
  output SCCout
);
endmodule

module CC (
  input  setCC,
  input  [63:0] valE,
  output [63:0] PCUpdate
);
endmodule
