// Logisim project Lab6.circ as structural Verilog: 2 circuits, main circuit main
module main (
);

  wire clock_1_out;

  ROM rom_1 ();  // open: addr, data
  Clock clock_1 (.out(clock_1_out));
  RAM ram_1 ();  // open: addr, we, oe, clk, din, dout
endmodule

module Fetch (
  input  [63:0] I,
  output [3:0] iCode,
  output [3:0] iFun,
  output [3:0] rA,
  output [3:0] rB,
  output [3:0] valC,
  output [3:0] valP
);
endmodule
